# Fritzing sketch INF1510_BALL2_0_v3 (saved by Fritzing 0.8.0b)
breadboards: 1

parts:
  VCC1 = Battery block 9V  # not connected
  GY2 = MPU-6050 Board GY-521 [form="♀ (female)" package=THT]  # not connected
  Part3 = SKGPS-53
  Part4 = Arduino Uno (Rev3)
  SD_card_module1 = SD Card Module

nets:
  N1: Part3.no_name_yet#connector5Vpin-0, SD_card_module1.+5
  N2: Part3.no_name_yet#connectorGNDpin-1, SD_card_module1.GND#7
  N3: Part4.ICSP_MISO, Part4.D12/MISO, SD_card_module1.MOSI
  N4: Part4.ICSP_MOSI, Part4.D11_PWM/MOSI, SD_card_module1.SCK
  N5: Part4.D10_PWM/SS, SD_card_module1.MISO

notes:
  Arduinoen skal:
  0. Få strøm fra batteriet.
  1. Måle akselrasjon/o den er i bevegelse.
  2. Hvert x sekund, find GPS posisjon
  3. Lagre data fra 1. og 2. til SD kortet
  OBS! Alle resistorer må sjekkes for riktig motstand!
  OBS! Viktig at gyro/acc har 3.3V og ikke 5V1

custom parts:
  MPU-6050 Board GY-521: Acelerometro y Giroscopio MPU-6050 Board GY-521
  SD Card Module: SD Card Module Slot Socket Reader For Arduino ARM MCU
